// Logisim project e2587921.circ as structural Verilog: 1 circuit, main circuit main
module main (
  input  A1,
  input  A0,
  input  B1,
  input  B0,
  input  O2,
  input  O1,
  input  O0,
  output L0,
  output L1,
  output L2,
  output L3,
  output L4,
  output L5,
  output L6,
  output S
);

  wire and_1_out, and_2_out, and_3_out, and_4_out, and_5_out, and_6_out, and_7_out, and_8_out, and_10_out,
       and_11_out, n3_to_8_decoder_74138_1_p1, n3_to_8_decoder_74138_1_p2, n3_to_8_decoder_74138_1_p3,
       n4_to_1_mux_x2_74153_1_p2, n4_to_1_mux_x2_74153_1_p4, n4_to_1_mux_x2_74153_1_p5,
       n4_to_1_mux_x2_74153_1_p6, n4_to_1_mux_x2_74153_1_p7, n4_to_1_mux_x2_74153_1_p8,
       n4_to_1_mux_x2_74153_1_p10, n4_to_1_mux_x2_74153_1_p11, n4_to_1_mux_x2_74153_2_p4,
       n4_to_1_mux_x2_74153_2_p5, n4_to_1_mux_x2_74153_2_p6, n4_to_1_mux_x2_74153_2_p7,
       n4_to_1_mux_x2_74153_2_p9, n4_to_1_mux_x2_74153_2_p10, n4_to_1_mux_x2_74153_2_p11,
       n4_to_1_mux_x2_74153_3_p4, n4_to_1_mux_x2_74153_3_p6, nand_1_out, not_1_out, not_2_out, not_3_out,
       not_4_out, or_2_out, or_3_out, or_7_out, or_8_out, or_9_out, xor_1_out, xor_2_out, xor_3_out,
       xor_6_out, xor_7_out;

  not not_1 (not_1_out, A1);
  not not_2 (not_2_out, A0);
  not not_3 (not_3_out, B1);
  not not_4 (not_4_out, B0);
  xor xor_1 (xor_1_out, A0, B0);
  // _4_to_1_MUX__x2___74153 #(.Facing("south")) 4_to_1_mux_x2_74153_1: pin names not known; wires that end beside it: O2, n4_to_1_mux_x2_74153_1_p2, xor_1_out, n4_to_1_mux_x2_74153_1_p4, n4_to_1_mux_x2_74153_1_p5, n4_to_1_mux_x2_74153_1_p6, n4_to_1_mux_x2_74153_1_p7, n4_to_1_mux_x2_74153_1_p8, n4_to_1_mux_x2_74153_1_p5, n4_to_1_mux_x2_74153_1_p10, n4_to_1_mux_x2_74153_1_p11, 1'b1, O0, O1
  not not_5 (n4_to_1_mux_x2_74153_1_p2, O2);
  // _3_to_8_decoder__74138 #(.Facing("south")) 3_to_8_decoder_74138_1: pin names not known; wires that end beside it: n3_to_8_decoder_74138_1_p1, n3_to_8_decoder_74138_1_p2, n3_to_8_decoder_74138_1_p3, 1'b1, 1'b0, 1'b0
  and and_1 (and_1_out, A0, B0);
  xor xor_2 (xor_2_out, A1, B1);
  xor xor_3 (xor_3_out, xor_2_out, and_1_out);
  or or_1 (n3_to_8_decoder_74138_1_p1, n4_to_1_mux_x2_74153_1_p4, n4_to_1_mux_x2_74153_1_p6);
  // NOT_Gate not_6 has open pins: in=open, out=L2
  // NOT_Gate not_7 has open pins: in=open, out=L4
  // NOT_Gate not_8 has open pins: in=open, out=L3
  // NOT_Gate not_9 has open pins: in=open, out=L5
  // NOT_Gate not_10 has open pins: in=open, out=L1
  // NOT_Gate not_11 has open pins: in=open, out=L6
  // NOT_Gate not_12 has open pins: in=open, out=L0
  and and_2 (and_2_out, A1, B1);
  and and_3 (and_3_out, xor_2_out, and_1_out);
  or or_2 (or_2_out, and_3_out, and_2_out);
  and and_4 (and_4_out, A0, B1);
  and and_5 (and_5_out, A1, B0);
  or or_3 (or_3_out, and_4_out, and_5_out);
  // _4_to_1_MUX__x2___74153 #(.Facing("south")) 4_to_1_mux_x2_74153_2: pin names not known; wires that end beside it: O2, n4_to_1_mux_x2_74153_1_p2, xor_3_out, n4_to_1_mux_x2_74153_2_p4, n4_to_1_mux_x2_74153_2_p5, n4_to_1_mux_x2_74153_2_p6, n4_to_1_mux_x2_74153_2_p7, 1'b0, n4_to_1_mux_x2_74153_2_p9, n4_to_1_mux_x2_74153_2_p10, n4_to_1_mux_x2_74153_2_p11, 1'b1, O0, O1
  or or_4 (n3_to_8_decoder_74138_1_p2, n4_to_1_mux_x2_74153_2_p4, n4_to_1_mux_x2_74153_2_p6);
  and and_6 (and_6_out, not_1_out, not_2_out);
  and and_7 (and_7_out, not_2_out, B1);
  or or_5 (n4_to_1_mux_x2_74153_2_p7, and_1_out, and_7_out);
  and and_8 (and_8_out, not_1_out, B0);
  and and_9 (n4_to_1_mux_x2_74153_1_p7, and_6_out, B0);
  // _4_to_1_MUX__x2___74153 #(.Facing("south")) 4_to_1_mux_x2_74153_3: pin names not known; wires that end beside it: O2, n4_to_1_mux_x2_74153_1_p2, or_2_out, n4_to_1_mux_x2_74153_3_p4, 1'b0, n4_to_1_mux_x2_74153_3_p6, or_3_out, 1'b0, 1'b0, 1'b0, 1'b0, 1'b1, O0, O1
  or or_6 (n3_to_8_decoder_74138_1_p3, n4_to_1_mux_x2_74153_3_p4, n4_to_1_mux_x2_74153_3_p6);
  and and_10 (and_10_out, B1, B0);
  and and_11 (and_11_out, not_1_out, B1);
  or or_7 (or_7_out, and_7_out, and_6_out);
  or or_8 (or_8_out, and_11_out, and_10_out);
  or or_9 (or_9_out, and_8_out, or_7_out);
  or or_10 (n4_to_1_mux_x2_74153_1_p8, or_9_out, or_8_out);
  xor xor_4 (n4_to_1_mux_x2_74153_2_p9, A1, B1);
  and and_12 (n4_to_1_mux_x2_74153_2_p10, A1, B1);
  xor xor_5 (n4_to_1_mux_x2_74153_1_p5, A0, B0);
  and and_13 (n4_to_1_mux_x2_74153_1_p10, A0, B0);
  nor nor_1 (n4_to_1_mux_x2_74153_2_p11, A1, B1);
  nor nor_2 (n4_to_1_mux_x2_74153_1_p11, A0, B0);
  xor xor_6 (xor_6_out, A1, A0);
  and and_14 (n4_to_1_mux_x2_74153_2_p5, n4_to_1_mux_x2_74153_2_p9, nand_1_out);
  not not_13 (S, n4_to_1_mux_x2_74153_1_p8);
  xor xor_7 (xor_7_out, B1, B0);
  nand nand_1 (nand_1_out, xor_6_out, xor_7_out);

  // Notes on the sheet:
  //   ADD
  //   ADDX0
  //   ADDX1
  //   ADDX2
  //   LSHIFT
  //   LSHX1
  //   LSHX2
  //   LSHX0
  //   GREQ
  //   GREQX0
  //   XOR
  //   XORX1
  //   AND
  //   XORX0
  //   ANDX1
  //   ANDX0
  //   NORX1
  //   NOR
  //   NORX0
  //   SUBX0
  //   SUBX1
endmodule
